// Logisim project Add4Bits.circ as structural Verilog: 2 circuits, main circuit main
module main (
  input  in_1,
  input  [3:0] in_2,
  input  [3:0] in_3,
  output [3:0] out_4,
  output out_5
);

  wire add1bit_1_out_5, add1bit_2_out_5, add1bit_3_out_5;

  Add1Bit add1bit_1 (.in_1(in_2[0]), .in_2(in_3[0]), .in_3(in_1), .out_4(out_4[0]), .out_5(add1bit_1_out_5));
  Add1Bit add1bit_2 (.in_1(in_2[1]), .in_2(in_3[1]), .in_3(add1bit_1_out_5), .out_4(out_4[1]), .out_5(add1bit_2_out_5));
  Add1Bit add1bit_3 (.in_1(in_2[2]), .in_2(in_3[2]), .in_3(add1bit_2_out_5), .out_4(out_4[2]), .out_5(add1bit_3_out_5));
  Add1Bit add1bit_4 (.in_1(in_2[3]), .in_2(in_3[3]), .in_3(add1bit_3_out_5), .out_4(out_4[3]), .out_5(out_5));
endmodule

module Add1Bit (
  input  in_1,
  input  in_2,
  input  in_3,
  output out_4,
  output out_5
);

  wire and_1_out, and_2_out, and_3_out, xor_1_out;

  xor xor_1 (xor_1_out, in_1, in_2);
  and and_1 (and_1_out, in_1, in_2);
  and and_2 (and_2_out, in_1, in_3);
  and and_3 (and_3_out, in_2, in_3);
  xor xor_2 (out_4, xor_1_out, in_3);
  or or_1 (out_5, and_1_out, and_2_out, and_3_out);
endmodule
