// Logisim project Lab2_ALU.circ as structural Verilog: 1 circuit, main circuit main
module main (
  input  [7:0] in_1,
  input  [7:0] in_2,
  input  [2:0] in_3,
  input  in_4,
  output [7:0] out_5
);

  wire [7:0] adder_1_out, and_1_out, bit_extender_1_out, multiplexer_1_out, not_1_out, or_1_out;

  Adder adder_1 (.a(in_1), .b(multiplexer_1_out), .out(adder_1_out), .cin(in_3[2]), .cout(in_4));
  assign or_1_out = multiplexer_1_out | in_1;  // OR_Gate or_1, 8 bits wide
  assign bit_extender_1_out = {{7{1'b0}}, adder_1_out[7]};  // Bit_Extender bit_extender_1
  assign not_1_out = ~in_2;  // NOT_Gate not_1, 8 bits wide
  Multiplexer #(.select(2), .width(8)) multiplexer_1 (
    .in0(in_2), .in1(in_2), .in2(not_1_out), .in3(not_1_out), .out(multiplexer_1_out), .sel(in_3[2:1]));
  assign and_1_out = multiplexer_1_out & in_1;  // AND_Gate and_1, 8 bits wide
  Multiplexer #(.select(2), .width(8)) multiplexer_2 (
    .in0(and_1_out), .in1(or_1_out), .in2(adder_1_out), .in3(bit_extender_1_out), .out(out_5), .sel(in_3[1:0]));

  // Notes on the sheet:
  //   F
  //   Adder
  //   B
  //   Shift
  //   A
  //   Negation
  //   Output Selection
endmodule
